# Fritzing sketch Automatic_Medicine_Reminder_with_LCD_RTC (saved by Fritzing 0.9.3b)
breadboards: 1

parts:
  ZS-042_RTC2 = ZS-042 RTC Module
  LCD2 = LCD screen  # not connected
  LCM1602_IIC3 = LCM1602 IIC [part_number="LCM1602 IIC" chip_label="LCM1602 IIC" package="DIP (Dual Inline) [THT]"]
  Part1 = Arduino Uno (Rev3)
  S1 = Pushbutton [package="[THT]"]
  S2 = Pushbutton [package="[THT]"]
  S3 = Pushbutton [package="[THT]"]
  S4 = Pushbutton [package="[THT]"]
  J1 = Piezo Speaker
  R1 = Resistor [tolerance=±5% resistance=220 package=THT]
  R2 = Resistor [tolerance=±5% resistance=220 package=THT]
  R3 = Resistor [tolerance=±5% resistance=220 package=THT]
  R4 = Resistor [tolerance=±5% resistance=220 package=THT]
  LED1 = smd LED [color="Red (660nm)" package="0603 [SMD]"]
  R6 = Resistor [tolerance=±5% resistance=220 package=THT]

nets:
  GND: ZS-042_RTC2.GND, LCM1602_IIC3.GND, Part1.GND, J1.pin1, R1.Pin_1, R2.Pin_1, R3.Pin_1, R4.Pin_1, R6.Pin_1
  VCC: ZS-042_RTC2.VCC, Part1.5V
  N1: ZS-042_RTC2.SDA, LCM1602_IIC3.SDA, Part1.A4/SDA
  N2: ZS-042_RTC2.SCL, LCM1602_IIC3.SCL, Part1.A5/SCL
  N3: LCM1602_IIC3.VCC, Part1.ioref
  N4: Part1.D9_PWM, S4.Pin_3, S4.Pin_4
  N5: Part1.D11_PWM/MOSI, J1.pin2
  N6: Part1.D13/SCK, LED1.anode
  N7: Part1.D2, S1.Pin_3, S1.Pin_4
  N8: Part1.D3_PWM, S2.Pin_3, S2.Pin_4
  N9: Part1.D4, S3.Pin_3, S3.Pin_4
  N10: S1.Pin_1, S1.Pin_2, R1.Pin_0
  N11: S2.Pin_1, S2.Pin_2, R4.Pin_0
  N12: S3.Pin_1, S3.Pin_2, R3.Pin_0
  N13: S4.Pin_1, S4.Pin_2, R2.Pin_0
  N14: LED1.cathode, R6.Pin_0

custom parts:
  LCM1602 IIC: I2C-Module to use a 1602 or 2004 LCD on with the wire.h libory Serial LCD Modul
